# Fritzing sketch schematics (saved by Fritzing 0.9.3b)

parts:
  MG90S_perna_esquerda = Basic Servo
  MG90S_perna_direita = Basic Servo
  MG90S_pé_direito = Basic Servo
  MG90S_pé_esquerdo = Basic Servo
  U1 = ESP8266 NodeMCU LoLin base
  hc-sr1 = hc-sr04
  SW1 = DPDT Switch [package="[THT]"]
  J1 = Piezo Speaker
  8x8_LED_Modul_mit_MAX1 = 8x8 LED Modul mit MAX7219 [package=THT]
  U2 = LIPO-1000mAh [package=lipo-1000]

nets:
  GND: MG90S_perna_esquerda.gnd, MG90S_perna_direita.gnd, MG90S_pé_direito.gnd, MG90S_pé_esquerdo.gnd, U1.GND1-0, U1.GND1-1, U1.GND1-2, U1.GND1-3, U1.GND2-0, U1.GND2-3, U1.GND3-0, U1.GND8-5, U1.GND8-6, U1.GND8-9, U1.GND8-10, hc-sr1.GND, J1.pin1, 8x8_LED_Modul_mit_MAX1.GND_Eingang, U2.-
  VCC: MG90S_perna_esquerda.vcc, MG90S_perna_direita.vcc, MG90S_pé_direito.vcc, MG90S_pé_esquerdo.vcc, U1.3V1-0, U1.3V1-1, U1.3V1-2, U1.3V1-3, U1.3V3-0, 8x8_LED_Modul_mit_MAX1.VCC_Eingang
  N1: MG90S_perna_esquerda.pulse, U1.D2-0, U1.D2-3
  N2: MG90S_perna_direita.pulse, U1.D3-0, U1.D3-3
  N3: MG90S_pé_direito.pulse, U1.D1-3
  N4: MG90S_pé_esquerdo.pulse, U1.D0-3
  N5: U1.D4-0, U1.D4-3, hc-sr1.Trig
  N6: U1.D5-0, U1.D5-3, hc-sr1.Echo
  N7: U1.D6-0, U1.D6-3, 8x8_LED_Modul_mit_MAX1.CLK_Eingang
  N8: U1.D7-1, U1.D7-3, 8x8_LED_Modul_mit_MAX1.CS_Eingang
  N9: U1.D8-2, U1.D8-3, 8x8_LED_Modul_mit_MAX1.DIN_Eingang
  N10: U1.RX-3, J1.pin2
  VIN: U1.VIN, U1.5V-3, hc-sr1.VCC
  N11: U1.UI-0, U1.UI-2, SW1.pin_4
  N12: SW1.common_2, U2.+

custom parts:
  ESP8266 NodeMCU LoLin base: ESP8266 based NodeMCU Base
  DPDT Switch: Standard DPDT push lock switch.
